// Logisim project Pila.circ as structural Verilog: 2 circuits, main circuit main
module main (
  input  in_1,
  input  in_2,
  input  [31:0] in_3,
  output [31:0] out_4
);

  wire controlled_buffer_1_out, controlled_buffer_3_out, counter_1_q, demultiplexer_1_out1, not_1_out,
       not_2_out, not_3_out;
  wire [31:0] _1, _2, _3, _4, _5, _6, _7, _8, _9, _10, _11, _12, _13, _14, _15, _16, _17, _18, _19, _20, _21,
       _22, _23, _24, _25, _26, _27, _28, _29, _30, _31, _32, controlled_buffer_2_out;

  not not_1 (not_1_out, in_2);
  assign controlled_buffer_1_out = not_2_out ? in_1 : 1'bz;  // Controlled_Buffer controlled_buffer_1
  not not_2 (not_2_out, in_2);
  assign controlled_buffer_2_out = not_1_out ? in_3 : 32'bz;  // Controlled_Buffer controlled_buffer_2
  Demultiplexer #(.disabled(0), .enable("false")) demultiplexer_1 (
    .out1(demultiplexer_1_out1), .in(controlled_buffer_1_out), .sel(counter_1_q));  // open: out0
  Counter #(.width(1), .max('h1)) counter_1 (.Q(counter_1_q), .clk(in_1));  // open: load, D, count, carry, clr
  Shift_Register #(.width(32), .length(32)) shift_register_1 (
    .in(controlled_buffer_2_out), .clk(demultiplexer_1_out1), .q0(_1), .q1(_2), .q2(_3), .q3(_4), .q4(_5),
    .q5(_6), .q6(_7), .q7(_8), .q8(_9), .q9(_10), .q10(_11), .q11(_12), .q12(_13), .q13(_14), .q14(_15),
    .q15(_16), .q16(_17), .q17(_18), .q18(_19), .q19(_20), .q20(_21), .q21(_22), .q22(_23), .q23(_24),
    .q24(_25), .q25(_26), .q26(_27), .q27(_28), .q28(_29), .q29(_30), .q30(_31), .q31(_32));  // open: shift, out, load, clr, d0, d1, d2, d3, d4, d5, d6, d7, d8, d9, d10, d11, d12, d13, d14, d15, d16, d17, d18, d19, d20, d21, d22, d23, d24, d25, d26, d27, d28, d29, d30, d31
  assign controlled_buffer_3_out = not_3_out ? 1'b1 : 1'bz;  // Controlled_Buffer controlled_buffer_3
  not not_3 (not_3_out, in_2);
  Shift_Register #(.width(32), .length(32)) shift_register_2 (
    .shift(in_2), .in({32{1'b0}}), .clk(in_1), .load(controlled_buffer_3_out), .d0(_32), .d1(_31), .d2(_30),
    .d3(_29), .d4(_28), .d5(_27), .d6(_26), .d7(_25), .d8(_24), .d9(_23), .d10(_22), .d11(_21), .d12(_20),
    .d13(_19), .d14(_18), .d15(_17), .d16(_16), .d17(_15), .d18(_14), .d19(_13), .d20(_12), .d21(_11),
    .d22(_10), .d23(_9), .d24(_8), .d25(_7), .d26(_6), .d27(_5), .d28(_4), .d29(_3), .d30(_2), .d31(_1),
    .q31(out_4));  // open: out, clr, q0, q1, q2, q3, q4, q5, q6, q7, q8, q9, q10, q11, q12, q13, q14, q15, q16, q17, q18, q19, q20, q21, q22, q23, q24, q25, q26, q27, q28, q29, q30

  // Other names for the same wires on the sheet: clk = in_1; Pop = in_2
endmodule

module Test (
  input  in_1,
  input  [31:0] in_2,
  output [31:0] out_3
);

  wire clock_1_out;

  Clock clock_1 (.out(clock_1_out));
  main main_1 (.in_2(in_1), .in_3(in_2), .out_4(out_3), .in_1(clock_1_out));
endmodule
