// Logisim project RegisterFile.circ as structural Verilog: 1 circuit, main circuit main
module main (
  input  [4:0] Selector_de_Registro,
  input  [31:0] Entrada,
  input  in_3,
  input  [4:0] Lectura_R1,
  input  [4:0] Lectura_R2,
  output [31:0] out_6,
  output [31:0] out_7
);

  wire and_1_out, and_2_out, and_3_out, and_4_out, and_5_out, and_6_out, and_7_out, and_8_out, and_9_out,
       and_10_out, and_11_out, and_12_out, and_13_out, and_14_out, and_15_out, and_16_out, and_17_out,
       and_18_out, and_19_out, and_20_out, and_21_out, and_22_out, and_23_out, and_24_out, and_25_out,
       and_26_out, and_27_out, and_28_out, and_29_out, and_30_out, and_31_out, and_32_out,
       demultiplexer_1_out0, demultiplexer_1_out1, demultiplexer_1_out2, demultiplexer_1_out3,
       demultiplexer_1_out4, demultiplexer_1_out5, demultiplexer_1_out6, demultiplexer_1_out7,
       demultiplexer_1_out8, demultiplexer_1_out9, demultiplexer_1_out10, demultiplexer_1_out11,
       demultiplexer_1_out12, demultiplexer_1_out13, demultiplexer_1_out14, demultiplexer_1_out15,
       demultiplexer_1_out16, demultiplexer_1_out17, demultiplexer_1_out18, demultiplexer_1_out19,
       demultiplexer_1_out20, demultiplexer_1_out21, demultiplexer_1_out22, demultiplexer_1_out23,
       demultiplexer_1_out24, demultiplexer_1_out25, demultiplexer_1_out26, demultiplexer_1_out27,
       demultiplexer_1_out28, demultiplexer_1_out29, demultiplexer_1_out30, demultiplexer_1_out31;
  wire [31:0] register_1_q, register_2_q, register_3_q, register_4_q, register_5_q, register_6_q,
       register_7_q, register_8_q, register_9_q, register_10_q, register_11_q, register_12_q, register_13_q,
       register_14_q, register_15_q, register_16_q, register_17_q, register_18_q, register_19_q,
       register_20_q, register_21_q, register_22_q, register_23_q, register_24_q, register_25_q,
       register_26_q, register_27_q, register_28_q, register_29_q, register_30_q, register_31_q,
       register_32_q;

  Demultiplexer #(.select(5), .enable("false")) demultiplexer_1 (
    .out0(demultiplexer_1_out0), .out1(demultiplexer_1_out1), .out2(demultiplexer_1_out2),
    .out3(demultiplexer_1_out3), .out4(demultiplexer_1_out4), .out5(demultiplexer_1_out5),
    .out6(demultiplexer_1_out6), .out7(demultiplexer_1_out7), .out8(demultiplexer_1_out8),
    .out9(demultiplexer_1_out9), .out10(demultiplexer_1_out10), .out11(demultiplexer_1_out11),
    .out12(demultiplexer_1_out12), .out13(demultiplexer_1_out13), .out14(demultiplexer_1_out14),
    .out15(demultiplexer_1_out15), .out16(demultiplexer_1_out16), .out17(demultiplexer_1_out17),
    .out18(demultiplexer_1_out18), .out19(demultiplexer_1_out19), .out20(demultiplexer_1_out20),
    .out21(demultiplexer_1_out21), .out22(demultiplexer_1_out22), .out23(demultiplexer_1_out23),
    .out24(demultiplexer_1_out24), .out25(demultiplexer_1_out25), .out26(demultiplexer_1_out26),
    .out27(demultiplexer_1_out27), .out28(demultiplexer_1_out28), .out29(demultiplexer_1_out29),
    .out30(demultiplexer_1_out30), .out31(demultiplexer_1_out31), .in(1'b1), .sel(Selector_de_Registro));
  and and_1 (and_1_out, demultiplexer_1_out0, 1'b1);
  and and_2 (and_2_out, demultiplexer_1_out1, 1'b1);
  and and_3 (and_3_out, demultiplexer_1_out2, 1'b1);
  and and_4 (and_4_out, demultiplexer_1_out3, 1'b1);
  and and_5 (and_5_out, demultiplexer_1_out4, 1'b1);
  and and_6 (and_6_out, demultiplexer_1_out5, 1'b1);
  and and_7 (and_7_out, demultiplexer_1_out6, 1'b1);
  and and_8 (and_8_out, demultiplexer_1_out7, 1'b1);
  and and_9 (and_9_out, demultiplexer_1_out8, 1'b1);
  and and_10 (and_10_out, demultiplexer_1_out9, 1'b1);
  and and_11 (and_11_out, demultiplexer_1_out10, 1'b1);
  and and_12 (and_12_out, demultiplexer_1_out11, 1'b1);
  and and_13 (and_13_out, demultiplexer_1_out12, 1'b1);
  and and_14 (and_14_out, demultiplexer_1_out13, 1'b1);
  and and_15 (and_15_out, demultiplexer_1_out14, 1'b1);
  and and_16 (and_16_out, demultiplexer_1_out15, 1'b1);
  Register #(.width(32)) register_1 (.D(Entrada), .en(and_1_out), .Q(register_1_q), .clk(in_3));  // open: clr
  Register #(.width(32)) register_2 (.D(Entrada), .en(and_2_out), .Q(register_2_q), .clk(in_3));  // open: clr
  Register #(.width(32)) register_3 (.D(Entrada), .en(and_3_out), .Q(register_3_q), .clk(in_3));  // open: clr
  Register #(.width(32)) register_4 (.D(Entrada), .en(and_4_out), .Q(register_4_q), .clk(in_3));  // open: clr
  Register #(.width(32)) register_5 (.D(Entrada), .en(and_5_out), .Q(register_5_q), .clk(in_3));  // open: clr
  Register #(.width(32)) register_6 (.D(Entrada), .en(and_6_out), .Q(register_6_q), .clk(in_3));  // open: clr
  Register #(.width(32)) register_7 (.D(Entrada), .en(and_7_out), .Q(register_7_q), .clk(in_3));  // open: clr
  Register #(.width(32)) register_8 (.D(Entrada), .en(and_8_out), .Q(register_8_q), .clk(in_3));  // open: clr
  Register #(.width(32)) register_9 (.D(Entrada), .en(and_9_out), .Q(register_9_q), .clk(in_3));  // open: clr
  Register #(.width(32)) register_10 (.D(Entrada), .en(and_10_out), .Q(register_10_q), .clk(in_3));  // open: clr
  Register #(.width(32)) register_11 (.D(Entrada), .en(and_11_out), .Q(register_11_q), .clk(in_3));  // open: clr
  Register #(.width(32)) register_12 (.D(Entrada), .en(and_12_out), .Q(register_12_q), .clk(in_3));  // open: clr
  Register #(.width(32)) register_13 (.D(Entrada), .en(and_13_out), .Q(register_13_q), .clk(in_3));  // open: clr
  Register #(.width(32)) register_14 (.D(Entrada), .en(and_14_out), .Q(register_14_q), .clk(in_3));  // open: clr
  Register #(.width(32)) register_15 (.D(Entrada), .en(and_15_out), .Q(register_15_q), .clk(in_3));  // open: clr
  Register #(.width(32)) register_16 (.D(Entrada), .en(and_16_out), .Q(register_16_q), .clk(in_3));  // open: clr
  and and_17 (and_17_out, demultiplexer_1_out16, 1'b1);
  and and_18 (and_18_out, demultiplexer_1_out17, 1'b1);
  and and_19 (and_19_out, demultiplexer_1_out18, 1'b1);
  and and_20 (and_20_out, demultiplexer_1_out19, 1'b1);
  and and_21 (and_21_out, demultiplexer_1_out20, 1'b1);
  and and_22 (and_22_out, demultiplexer_1_out21, 1'b1);
  and and_23 (and_23_out, demultiplexer_1_out22, 1'b1);
  and and_24 (and_24_out, demultiplexer_1_out23, 1'b1);
  and and_25 (and_25_out, demultiplexer_1_out24, 1'b1);
  and and_26 (and_26_out, demultiplexer_1_out25, 1'b1);
  and and_27 (and_27_out, demultiplexer_1_out26, 1'b1);
  and and_28 (and_28_out, demultiplexer_1_out27, 1'b1);
  and and_29 (and_29_out, demultiplexer_1_out28, 1'b1);
  and and_30 (and_30_out, demultiplexer_1_out29, 1'b1);
  and and_31 (and_31_out, demultiplexer_1_out30, 1'b1);
  and and_32 (and_32_out, demultiplexer_1_out31, 1'b1);
  Register #(.width(32)) register_17 (.D(Entrada), .en(and_17_out), .Q(register_17_q), .clk(in_3));  // open: clr
  Register #(.width(32)) register_18 (.D(Entrada), .en(and_18_out), .Q(register_18_q), .clk(in_3));  // open: clr
  Register #(.width(32)) register_19 (.D(Entrada), .en(and_19_out), .Q(register_19_q), .clk(in_3));  // open: clr
  Register #(.width(32)) register_20 (.D(Entrada), .en(and_20_out), .Q(register_20_q), .clk(in_3));  // open: clr
  Register #(.width(32)) register_21 (.D(Entrada), .en(and_21_out), .Q(register_21_q), .clk(in_3));  // open: clr
  Register #(.width(32)) register_22 (.D(Entrada), .en(and_22_out), .Q(register_22_q), .clk(in_3));  // open: clr
  Register #(.width(32)) register_23 (.D(Entrada), .en(and_23_out), .Q(register_23_q), .clk(in_3));  // open: clr
  Register #(.width(32)) register_24 (.D(Entrada), .en(and_24_out), .Q(register_24_q), .clk(in_3));  // open: clr
  Register #(.width(32)) register_25 (.D(Entrada), .en(and_25_out), .Q(register_25_q), .clk(in_3));  // open: clr
  Register #(.width(32)) register_26 (.D(Entrada), .en(and_26_out), .Q(register_26_q), .clk(in_3));  // open: clr
  Register #(.width(32)) register_27 (.D(Entrada), .en(and_27_out), .Q(register_27_q), .clk(in_3));  // open: clr
  Register #(.width(32)) register_28 (.D(Entrada), .en(and_28_out), .Q(register_28_q), .clk(in_3));  // open: clr
  Register #(.width(32)) register_29 (.D(Entrada), .en(and_29_out), .Q(register_29_q), .clk(in_3));  // open: clr
  Register #(.width(32)) register_30 (.D(Entrada), .en(and_30_out), .Q(register_30_q), .clk(in_3));  // open: clr
  Register #(.width(32)) register_31 (.D(Entrada), .en(and_31_out), .Q(register_31_q), .clk(in_3));  // open: clr
  Register #(.width(32)) register_32 (.D(Entrada), .en(and_32_out), .Q(register_32_q), .clk(in_3));  // open: clr
  Multiplexer #(.select(5), .width(32)) multiplexer_1 (
    .in0(register_1_q), .in1(register_2_q), .in2(register_3_q), .in3(register_4_q), .in4(register_5_q),
    .in5(register_6_q), .in6(register_7_q), .in7(register_8_q), .in8(register_9_q), .in9(register_10_q),
    .in10(register_11_q), .in11(register_12_q), .in12(register_13_q), .in13(register_14_q),
    .in14(register_15_q), .in15(register_16_q), .in16(register_17_q), .in17(register_18_q),
    .in18(register_19_q), .in19(register_20_q), .in20(register_21_q), .in21(register_22_q),
    .in22(register_23_q), .in23(register_24_q), .in24(register_25_q), .in25(register_26_q),
    .in26(register_27_q), .in27(register_28_q), .in28(register_29_q), .in29(register_30_q),
    .in30(register_31_q), .in31(register_32_q), .out(out_6), .sel(Lectura_R1));  // open: en
  Multiplexer #(.select(5), .width(32)) multiplexer_2 (
    .in0(register_17_q), .in1(register_18_q), .in2(register_19_q), .in3(register_20_q), .in4(register_21_q),
    .in5(register_22_q), .in6(register_23_q), .in7(register_24_q), .in8(register_25_q), .in9(register_26_q),
    .in10(register_27_q), .in11(register_28_q), .in12(register_29_q), .in13(register_30_q),
    .in14(register_31_q), .in15(register_32_q), .in16(register_1_q), .in17(register_2_q),
    .in18(register_3_q), .in19(register_4_q), .in20(register_5_q), .in21(register_6_q), .in22(register_7_q),
    .in23(register_8_q), .in24(register_9_q), .in25(register_10_q), .in26(register_10_q),
    .in27(register_11_q), .in28(register_12_q), .in29(register_13_q), .in30(register_14_q),
    .in31(register_15_q), .out(out_7), .sel(Lectura_R2));  // open: en
endmodule
