// Logisim project BigASM.circ as structural Verilog
module BOARD_BIG_ASM (
  output out_1
);

  wire button_1_out, CLK, CLR, d_ff_1_q, not_1_out, Write, Write_ASCII;
  wire [6:0] ASCII;
  wire [7:0] counter_1_q;
  wire [23:0] Dir_INPUT, Dir_MEMORY;
  wire [31:0] INPUT, MEMORY_IN, MEMORY_OUT;

  Button button_1 (.out(button_1_out));
  Clock clock_1 (.out(CLK));
  D_Flip_Flop d_ff_1 (.clk(CLK), .D(1'b1), .Q(d_ff_1_q), .reset(button_1_out));  // open: Qn, preset, en
  D_Flip_Flop d_ff_2 (.clk(CLK), .D(d_ff_1_q), .Qn(CLR), .reset(button_1_out));  // open: Q, preset, en
  BIG_ASM big_asm_1 (
    .DATA_INPUT(INPUT), .MEMORY_IN(MEMORY_OUT), .CLK(CLK), .CLR(CLR), .DIR_INPUT(Dir_INPUT),
    .MEMORY_OUT(MEMORY_IN), .DIR_MEMORY(Dir_MEMORY), .Write_OUTPUT(Write), .ASCII(ASCII),
    .Write_ASCII(Write_ASCII), .END(out_1));  // open: out_14, out_15, out_13, out_10
  MEMORY memory_1 (.DIR(Dir_MEMORY), .DATA_IN(MEMORY_IN), .WRITE(Write), .CLK(CLK), .CLR(CLR), .DATA_OUT(MEMORY_OUT));
  INPUT input_1 (.DIR(Dir_INPUT), .CLK(CLK), .DATA_OUT(INPUT));
  Counter counter_1 (.load(1'b0), .count(not_1_out), .Q(counter_1_q), .clk(CLK), .clr(CLR));  // open: D, carry
  not not_1 (not_1_out, out_1);
  // Probe on counter_1_q
  TTY #(.rows(32), .cols(60)) tty_1 (.data(ASCII), .clk(CLK), .we(Write_ASCII), .clr(CLR));

  // Other names for the same wires on the sheet: END = out_1

  // Notes on the sheet:
  //   COUNTER
  //   BOARD
endmodule

module INPUT (
  input  [23:0] DIR,
  input  CLK,
  output [31:0] DATA_OUT
);

  RAM #(.addrWidth(24), .dataWidth(32)) ram_1 (.addr(DIR), .data(DATA_OUT), .clk(CLK), .ld(1'b1));  // open: sel, clr
endmodule

module MEMORY (
  input  [23:0] DIR,
  input  [31:0] DATA_IN,
  input  WRITE,
  input  CLK,
  input  CLR,
  output [31:0] DATA_OUT
);

  RAM #(.addrWidth(24), .dataWidth(32), .bus("separate")) ram_1 (
    .addr(DIR), .din(DATA_IN), .data(DATA_OUT), .str(WRITE), .clk(CLK), .clr(CLR));  // open: sel, ld
endmodule

module BIG_ASM (
  input  [31:0] DATA_INPUT,
  input  [31:0] MEMORY_IN,
  input  CLK,
  input  CLR,
  output [23:0] DIR_INPUT,
  output [31:0] MEMORY_OUT,
  output [23:0] DIR_MEMORY,
  output Write_OUTPUT,
  output [6:0] ASCII,
  output [31:0] out_10,
  output Write_ASCII,
  output END,
  output [31:0] out_13,
  output [31:0] out_14,
  output [31:0] out_15
);

  wire A____B, A___B, and_1_out, Comienza, controlunit_1_l_a, controlunit_1_l_b, controlunit_1_s_a, EndPrint,
       not_2_out, or_1_out, RST_Print, start, startPrint, startPrint_2;
  wire [1:0] controlunit_1_s_b;
  wire [31:0] b_t, c, multiplexer_1_out;

  not not_1 (start, CLR);
  and and_1 (and_1_out, Comienza, start);
  ControlUnit controlunit_1 (
    .clk(CLK), .start(and_1_out), .A___B(A___B), .L_B(controlunit_1_l_b), .S_A(controlunit_1_s_a),
    .S_B(controlunit_1_s_b), .L_A(controlunit_1_l_a), .A____B(A____B), .EndPrint(EndPrint),
    .startPrint(startPrint), .startPrint2(startPrint_2), .EndPrint2(EndPrint), .RST(CLR), .END(END),
    .RST_Print(RST_Print));
  Counter #(.width(24), .max('hffffff)) counter_1 (
    .count(not_2_out), .Q(DIR_INPUT), .clk(CLK));  // open: load, D, carry, clr
  Multiplexer #(.width(32), .enable("false")) multiplexer_1 (
    .in0(out_15), .in1(out_14), .out(multiplexer_1_out), .sel(startPrint));
  or or_1 (or_1_out, startPrint, startPrint_2);
  Shift_Register #(.width(32), .length(4)) shift_register_1 (
    .shift(not_2_out), .in(DATA_INPUT), .clk(CLK), .q0(out_13), .q1(c), .q2(b_t), .q3(out_10));  // open: out, load, clr, d0, d1, d2, d3
  not not_2 (not_2_out, Comienza);
  Comparator #(.width(24), .mode("unsigned")) comparator_1 (.a(DIR_INPUT), .b(24'h3), .gt(Comienza));  // open: eq, lt
  PRINT_DEC print_dec_1 (
    .num(multiplexer_1_out), .start(or_1_out), .CLK(CLK), .RST(CLR), .ASCII(ASCII),
    .Write_ASCII(Write_ASCII), .END(EndPrint));
  DataPath datapath_1 (
    .in_1(out_10), .in_7(CLK), .in_2(c), .in_3(b_t), .in_4(out_13), .out_10(A____B), .out_11(A___B),
    .in_5(controlunit_1_l_a), .in_8(controlunit_1_l_b), .in_6(controlunit_1_s_a), .in_9(controlunit_1_s_b),
    .A(out_14), .B(out_15));

  // Other names for the same wires on the sheet: A[31:0] = out_14; a_t[31:0] = out_10; B[31:0] = out_15;
  //   d[31:0] = out_13; RST = CLR
endmodule

module PRINT_UDEC (
  input  [31:0] num,
  input  start,
  input  CLK,
  input  RST,
  output [6:0] ASCII,
  output Write_ASCII,
  output \end 
);

  wire _0_c, _0_n, demultiplexer_1_out0, demultiplexer_2_out0, demultiplexer_2_out1, demultiplexer_3_out0,
       demultiplexer_3_out1, IDLE_2_q, IDLE_3_q, IDLE_4_q, IDLE_q, Lc, Lc_0, Ln, Ln_0, or_1_out;
  wire [23:0] bit_extender_1_out;
  wire [31:0] c, c___1, c___1_t, divider_1_rem, memory_1_data_out, multiplexer_1_out, multiplexer_2_out,
       multiplexer_3_out, n, n___10, n___10___48;

  Multiplexer #(.width(32), .enable("false")) multiplexer_1 (
    .in0(num), .in1(n___10), .out(multiplexer_1_out), .sel(Lc_0));
  Divider #(.width(32)) divider_1 (.a(n), .b(32'ha), .out(n___10), .rem(divider_1_rem));  // open: upper
  Adder #(.width(32)) adder_1 (.a(divider_1_rem), .b(32'h30), .out(n___10___48));  // open: cin, cout
  or or_1 (or_1_out, demultiplexer_1_out0, \end );
  Register #(.width(32)) u_n (.D(multiplexer_1_out), .en(Ln), .Q(n), .clk(CLK), .clr(RST));
  D_Flip_Flop IDLE (.clk(CLK), .D(or_1_out), .Q(IDLE_q), .preset(RST));  // open: Qn, en, reset
  Demultiplexer #(.enable("false")) demultiplexer_1 (
    .out0(demultiplexer_1_out0), .out1(Ln_0), .in(IDLE_q), .sel(start));
  or or_2 (Write_ASCII, demultiplexer_3_out0, demultiplexer_2_out1);
  Multiplexer #(.width(32), .enable("false")) multiplexer_2 (
    .in0(c___1), .in1(c___1_t), .out(multiplexer_2_out), .sel(Write_ASCII));
  Adder #(.width(32)) adder_2 (.a(c), .b(32'h1), .out(c___1));  // open: cin, cout
  Subtractor #(.width(32)) subtractor_1 (.a(c), .b(32'h1), .out(c___1_t));  // open: bin, bout
  D_Flip_Flop IDLE_2 (.clk(CLK), .D(Ln_0), .Q(IDLE_2_q), .reset(RST));  // open: Qn, preset, en
  Register #(.width(32)) u_c (.D(multiplexer_2_out), .en(Lc), .Q(c), .clk(CLK), .clr(RST));
  or or_3 (Lc_0, IDLE_2_q, demultiplexer_3_out1);
  Multiplexer #(.width(32), .enable("false")) multiplexer_3 (
    .in0(c), .in1(c___1_t), .out(multiplexer_3_out), .sel(Write_ASCII));
  Comparator #(.width(32), .mode("unsigned")) comparator_1 (.a({32{1'b0}}), .b(n), .lt(_0_n));  // open: gt, eq
  Comparator #(.width(32), .mode("unsigned")) comparator_2 (.a({32{1'b0}}), .b(c), .lt(_0_c));  // open: gt, eq
  D_Flip_Flop IDLE_3 (.clk(CLK), .D(Write_ASCII), .Q(IDLE_3_q), .reset(RST));  // open: Qn, preset, en
  Demultiplexer #(.enable("false")) demultiplexer_2 (
    .out0(demultiplexer_2_out0), .out1(demultiplexer_2_out1), .in(IDLE_3_q), .sel(_0_c));
  Bit_Extender #(.in_width(32), .out_width(24)) bit_extender_1 (.in(multiplexer_3_out), .out(bit_extender_1_out));
  D_Flip_Flop IDLE_4 (.clk(CLK), .D(Lc_0), .Q(IDLE_4_q), .reset(RST));  // open: Qn, preset, en
  or or_4 (Lc, Lc_0, Write_ASCII);
  or or_5 (Ln, Ln_0, Lc_0);
  Demultiplexer #(.enable("false")) demultiplexer_3 (
    .out0(demultiplexer_3_out0), .out1(demultiplexer_3_out1), .in(IDLE_4_q), .sel(_0_n));
  D_Flip_Flop IDLE_5 (.clk(CLK), .D(demultiplexer_2_out0), .Q(\end ), .reset(RST));  // open: Qn, preset, en
  MEMORY memory_1 (
    .DIR(bit_extender_1_out), .DATA_IN(n___10___48), .WRITE(Lc_0), .CLK(CLK), .CLR(RST),
    .DATA_OUT(memory_1_data_out));
  Bit_Extender #(.in_width(32), .out_width(7)) bit_extender_2 (.in(memory_1_data_out), .out(ASCII));

  // Other names for the same wires on the sheet: Lc_1 = Write_ASCII; Sc = Write_ASCII; Ln_1 = Lc_0; Sn = Lc_0;
  //   Write = Lc_0
endmodule

module PRINT_DEC (
  input  [31:0] num,
  input  start,
  input  CLK,
  input  RST,
  output [6:0] ASCII,
  output Write_ASCII,
  output END
);

  wire demultiplexer_1_out0, demultiplexer_1_out1, demultiplexer_2_out0, demultiplexer_3_out0, end_t,
       IDLE_3_q, IDLE_q, or_1_out, or_2_out, or_3_out, S_ASCII, startUDEC, Write_ASCII_1;
  wire [6:0] ASCII_t;
  wire [31:0] multiplexer_1_out, negator_1_out;

  or or_1 (or_1_out, demultiplexer_1_out0, END);
  Negator #(.width(32)) negator_1 (.in(num), .out(negator_1_out));
  D_Flip_Flop IDLE (.clk(CLK), .D(or_1_out), .Q(IDLE_q), .preset(RST));  // open: Qn, en, reset
  Demultiplexer #(.enable("false")) demultiplexer_1 (
    .out0(demultiplexer_1_out0), .out1(demultiplexer_1_out1), .in(IDLE_q), .sel(start));
  Multiplexer #(.width(32), .enable("false")) multiplexer_1 (
    .in0(num), .in1(negator_1_out), .out(multiplexer_1_out), .sel(num[31]));
  Demultiplexer #(.enable("false")) demultiplexer_2 (
    .out0(demultiplexer_2_out0), .out1(S_ASCII), .in(demultiplexer_1_out1), .sel(num[31]));
  or or_2 (or_2_out, demultiplexer_2_out0, S_ASCII);
  D_Flip_Flop IDLE_2 (.clk(CLK), .D(or_2_out), .Q(startUDEC), .reset(RST));  // open: Qn, preset, en
  PRINT_UDEC print_udec_1 (
    .num(multiplexer_1_out), .start(startUDEC), .CLK(CLK), .RST(RST), .ASCII(ASCII_t),
    .Write_ASCII(Write_ASCII_1), .\end (end_t));
  D_Flip_Flop IDLE_3 (.clk(CLK), .D(or_3_out), .Q(IDLE_3_q), .reset(RST));  // open: Qn, preset, en
  or or_3 (or_3_out, startUDEC, demultiplexer_3_out0);
  Demultiplexer #(.enable("false")) demultiplexer_3 (
    .out0(demultiplexer_3_out0), .out1(END), .in(IDLE_3_q), .sel(end_t));
  Multiplexer #(.width(7), .enable("false")) multiplexer_2 (
    .in0(ASCII_t), .in1(7'b0101101), .out(ASCII), .sel(S_ASCII));
  or or_4 (Write_ASCII, S_ASCII, Write_ASCII_1);

  // Other names for the same wires on the sheet: sign = num[31]; Write_ASCII_0 = S_ASCII
endmodule

module TEST_PRINT (
  input  [31:0] in_1,
  output out_2
);

  wire button_1_out, button_2_out, CLK, CLR, d_ff_1_q, Write_ASCII;
  wire [6:0] ASCII;

  Button button_1 (.out(button_1_out));
  Clock clock_1 (.out(CLK));
  D_Flip_Flop d_ff_1 (.clk(CLK), .D(1'b1), .Q(d_ff_1_q), .reset(button_1_out));  // open: Qn, preset, en
  D_Flip_Flop d_ff_2 (.clk(CLK), .D(d_ff_1_q), .Qn(CLR), .reset(button_1_out));  // open: Q, preset, en
  Button button_2 (.out(button_2_out));
  PRINT_UDEC print_udec_1 ();  // open: num, start, CLK, RST, ASCII, Write_ASCII, end
  PRINT_DEC print_dec_1 (
    .num(in_1), .start(button_2_out), .CLK(CLK), .RST(CLR), .ASCII(ASCII), .Write_ASCII(Write_ASCII),
    .END(out_2));
  TTY #(.rows(32), .cols(60)) tty_1 (.data(ASCII), .clk(CLK), .we(Write_ASCII), .clr(CLR));
endmodule

module DataPath (
  input  [31:0] in_1,
  input  [31:0] in_2,
  input  [31:0] in_3,
  input  [31:0] in_4,
  input  in_5,
  input  in_6,
  input  in_7,
  input  in_8,
  input  [1:0] in_9,
  output out_10,
  output out_11,
  output [31:0] A,
  output [31:0] B
);

  wire comparator_3_eq, Den_Neg, Num_Neg, xor_1_out;
  wire [31:0] A_t, B___A, B_t, Den, Den_F, divider_1_out, multiplexer_3_out, multiplexer_4_out,
       negator_1_out, negator_2_out, negator_3_out, Num, Num_F;

  Multiplier #(.width(32)) multiplier_1 (.a(in_1), .b(in_2), .out(Num));  // open: cin, cout
  Multiplier #(.width(32)) multiplier_2 (.a(in_3), .b(in_4), .out(Den));  // open: cin, cout
  Negator #(.width(32)) negator_1 (.in(Den), .out(negator_1_out));
  Multiplexer #(.width(32), .enable("false")) multiplexer_1 (
    .in0(Num), .in1(negator_2_out), .out(Num_F), .sel(Num_Neg));
  Negator #(.width(32)) negator_2 (.in(Num), .out(negator_2_out));
  Comparator #(.width(32)) comparator_1 (.a(Num), .b({32{1'b0}}), .lt(Num_Neg));  // open: gt, eq
  Multiplexer #(.width(32), .enable("false")) multiplexer_2 (
    .in0(Den), .in1(negator_1_out), .out(Den_F), .sel(Den_Neg));
  Comparator #(.width(32)) comparator_2 (.a(Den), .b({32{1'b0}}), .lt(Den_Neg));  // open: gt, eq
  Multiplexer #(.width(32), .enable("false")) multiplexer_3 (
    .in0(Num_F), .in1(B_t), .out(multiplexer_3_out), .sel(in_6));
  Multiplexer #(.select(2), .width(32), .enable("false")) multiplexer_4 (
    .in0(Den_F), .in1(A_t), .in2(B___A), .in3(A_t), .out(multiplexer_4_out), .sel(in_9));
  Comparator #(.width(32), .mode("unsigned")) comparator_3 (
    .a(A_t), .b(B_t), .gt(out_11), .eq(comparator_3_eq));  // open: lt
  Register #(.width(32)) R1 (.D(multiplexer_3_out), .en(in_5), .Q(A_t), .clk(in_7));  // open: clr
  Register #(.width(32)) R1_2 (.D(multiplexer_4_out), .en(in_8), .Q(B_t), .clk(in_7));  // open: clr
  not not_1 (out_10, comparator_3_eq);
  Divider #(.width(32)) divider_1 (.a(Num_F), .b(A_t), .out(divider_1_out));  // open: upper, rem
  Divider #(.width(32)) divider_2 (.a(Den_F), .b(A_t), .out(B));  // open: upper, rem
  Subtractor #(.width(32)) subtractor_1 (.a(B_t), .b(A_t), .out(B___A));  // open: bin, bout
  Negator #(.width(32)) negator_3 (.in(divider_1_out), .out(negator_3_out));
  xor xor_1 (xor_1_out, Num_Neg, Den_Neg);
  Multiplexer #(.width(32), .enable("false")) multiplexer_5 (
    .in0(divider_1_out), .in1(negator_3_out), .out(A), .sel(xor_1_out));

  // Other names for the same wires on the sheet: A____B = out_10; A___B = out_11; a_t_t[31:0] = in_1;
  //   b_t_t[31:0] = in_3; c[31:0] = in_2; CLK = in_7; d[31:0] = in_4; L_A = in_5; L_B = in_8; S_A = in_6;
  //   S_B[1:0] = in_9
endmodule

module ControlUnit (
  input  clk,
  input  start,
  input  RST,
  input  A____B,
  input  A___B,
  input  EndPrint,
  input  EndPrint2,
  output L_A,
  output L_B,
  output S_A,
  output [1:0] S_B,
  output END,
  output startPrint,
  output startPrint2,
  output RST_Print
);

  wire d_ff_1_q, d_ff_2_q, d_ff_3_q, d_ff_5_q, demultiplexer_1_out0, demultiplexer_2_out0,
       demultiplexer_2_out1, demultiplexer_3_out0, demultiplexer_4_out0, demultiplexer_5_out0,
       demultiplexer_5_out1, L_A0, or_1_out, or_6_out, or_8_out, RST_print_1;

  D_Flip_Flop d_ff_1 (.clk(clk), .D(demultiplexer_1_out0), .Q(d_ff_1_q), .preset(RST));  // open: Qn, en, reset
  Demultiplexer #(.enable("false")) demultiplexer_1 (
    .out0(demultiplexer_1_out0), .out1(L_A0), .in(d_ff_1_q), .sel(start));
  or or_1 (or_1_out, L_A0, S_B[1]);
  or or_2 (L_A, L_A0, S_A);
  or or_3 (L_B, L_A0, S_A, S_B[1]);
  Demultiplexer #(.enable("false")) demultiplexer_2 (
    .out0(demultiplexer_2_out0), .out1(demultiplexer_2_out1), .in(d_ff_2_q), .sel(A____B));
  D_Flip_Flop d_ff_2 (.clk(clk), .D(or_1_out), .Q(d_ff_2_q));  // open: Qn, preset, en, reset
  Demultiplexer #(.enable("false")) demultiplexer_3 (
    .out0(demultiplexer_3_out0), .out1(S_A), .in(demultiplexer_2_out1), .sel(A___B));
  D_Flip_Flop d_ff_3 (.clk(clk), .D(startPrint), .Q(d_ff_3_q), .reset(RST));  // open: Qn, preset, en
  or or_4 (startPrint, demultiplexer_4_out0, demultiplexer_2_out0);
  buf or_5 (RST_Print, RST_print_1);  // OR_Gate
  Demultiplexer #(.enable("false")) demultiplexer_4 (
    .out0(demultiplexer_4_out0), .out1(RST_print_1), .in(d_ff_3_q), .sel(EndPrint));
  or or_6 (or_6_out, demultiplexer_3_out0, S_A);
  or or_7 (startPrint2, demultiplexer_5_out0, RST_print_1);
  D_Flip_Flop d_ff_4 (.clk(clk), .D(or_6_out), .Q(S_B[1]));  // open: Qn, preset, en, reset
  D_Flip_Flop d_ff_5 (.clk(clk), .D(startPrint2), .Q(d_ff_5_q), .reset(RST));  // open: Qn, preset, en
  Demultiplexer #(.enable("false")) demultiplexer_5 (
    .out0(demultiplexer_5_out0), .out1(demultiplexer_5_out1), .in(d_ff_5_q), .sel(EndPrint2));
  D_Flip_Flop d_ff_6 (.clk(clk), .D(or_8_out), .Q(END));  // open: Qn, preset, en, reset
  or or_8 (or_8_out, END, demultiplexer_5_out1);

  assign S_B[0] = S_A;

  // Other names for the same wires on the sheet: L_B0 = L_A0; L_A1 = S_A; L_B1 = S_A; S_B0 = S_A; L_B2 = S_B[1]
endmodule
