// Logisim project BigASM.circ as structural Verilog
module BOARD_BIG_ASM (
  output out_1
);

  wire button_1_out, CLK, CLR, d_ff_1_q, not_1_out, Write, Write_ASCII;
  wire [6:0] ASCII;
  wire [7:0] counter_1_q;
  wire [23:0] Dir_INPUT, Dir_MEMORY;
  wire [31:0] INPUT, MEMORY_IN, MEMORY_OUT;

  Button button_1 (.out(button_1_out));
  Clock clock_1 (.out(CLK));
  D_Flip_Flop d_ff_1 (.clk(CLK), .D(1'b1), .Q(d_ff_1_q), .reset(button_1_out));  // open: Qn, preset, en
  D_Flip_Flop d_ff_2 (.clk(CLK), .D(d_ff_1_q), .Qn(CLR), .reset(button_1_out));  // open: Q, preset, en
  BIG_ASM big_asm_1 (
    .DATA_INPUT(INPUT), .MEMORY_IN(MEMORY_OUT), .CLK(CLK), .CLR(CLR), .DIR_INPUT(Dir_INPUT),
    .MEMORY_OUT(MEMORY_IN), .DIR_MEMORY(Dir_MEMORY), .Write_OUTPUT(Write), .ASCII(ASCII),
    .Write_ASCII(Write_ASCII), .END(out_1));
  MEMORY memory_1 (.DIR(Dir_MEMORY), .DATA_IN(MEMORY_IN), .WRITE(Write), .CLK(CLK), .CLR(CLR), .DATA_OUT(MEMORY_OUT));
  INPUT input_1 (.DIR(Dir_INPUT), .CLK(CLK), .DATA_OUT(INPUT));
  Counter counter_1 (.load(1'b0), .count(not_1_out), .Q(counter_1_q), .clk(CLK), .clr(CLR));  // open: D, carry
  not not_1 (not_1_out, out_1);
  // Probe on counter_1_q
  TTY #(.rows(32), .cols(60)) tty_1 (.data(ASCII), .clk(CLK), .we(Write_ASCII), .clr(CLR));

  // Other names for the same wires on the sheet: END = out_1

  // Notes on the sheet:
  //   COUNTER
  //   BOARD
endmodule

module INPUT (
  input  [23:0] DIR,
  input  CLK,
  output [31:0] DATA_OUT
);

  RAM #(.addrWidth(24), .dataWidth(32)) ram_1 (.addr(DIR), .data(DATA_OUT), .clk(CLK), .ld(1'b1));  // open: sel, clr
endmodule

module MEMORY (
  input  [23:0] DIR,
  input  [31:0] DATA_IN,
  input  WRITE,
  input  CLK,
  input  CLR,
  output [31:0] DATA_OUT
);

  wire not_1_out;

  not not_1 (not_1_out, WRITE);
  RAM #(.addrWidth(24), .dataWidth(32), .bus("separate")) ram_1 (
    .addr(DIR), .din(DATA_IN), .data(DATA_OUT), .clk(CLK), .ld(not_1_out), .clr(CLR));  // open: str, sel
endmodule

module BIG_ASM (
  input  [31:0] DATA_INPUT,
  input  [31:0] MEMORY_IN,
  input  CLK,
  input  CLR,
  output [23:0] DIR_INPUT,
  output [31:0] MEMORY_OUT,
  output [23:0] DIR_MEMORY,
  output Write_OUTPUT,
  output [6:0] ASCII,
  output Write_ASCII,
  output END
);

  wire CLK_t, Cond1, Cond2, Cond3, Cond_int, Cont_Lec, Dec_Max, EndPrint, Mod_M, RSTPrint, start, StartPrint;
  wire [1:0] SI, SJ;
  wire [31:0] Lectura;

  not not_1 (start, CLR);
  Clock clock_1 (.out(CLK_t));
  ControlUnit controlunit_1 (
    .CLK(CLK_t), .Start(start), .SI(SI), .SJ(SJ), .Mod_M(Mod_M), .Cond2(Cond2), .Cond1(Cond1),
    .Cond_int(Cond_int), .Cond_3(Cond3), .Dec_Max(Dec_Max), .RST(CLR), .Cont_Lec(Cont_Lec),
    .EndPrint(EndPrint), .RSTPrint(RSTPrint), .StartPrint(StartPrint), .END(END));
  PRINT_DEC print_dec_1 (
    .num(Lectura), .start(StartPrint), .CLK(CLK_t), .RST(CLR), .ASCII(ASCII), .Write_ASCII(Write_ASCII),
    .END(EndPrint));
  DataPath datapath_1 (
    .CLK(CLK_t), .Condicional_Interna(Cond_int), .SI(SI), .SJ(SJ), .Mod_M(Mod_M), .Cond_2(Cond2),
    .Cond_1(Cond1), .CLR(CLR), .Cond_3(Cond3), .Lectura2(Lectura), .Cont_Lec(Cont_Lec), .Input(DATA_INPUT),
    .Max_Dec(Dec_Max));  // open: Array_Guardado, out_19, out_20, out_16, out_17, out_21, in_9, in_10

  assign DIR_INPUT = {24{1'b0}};

  // Other names for the same wires on the sheet: Input[31:0] = DATA_INPUT; RST = CLR
endmodule

module PRINT_UDEC (
  input  [31:0] num,
  input  start,
  input  CLK,
  input  RST,
  output [6:0] ASCII,
  output Write_ASCII,
  output \end 
);

  wire _0_c, _0_n, demultiplexer_1_out0, demultiplexer_2_out0, demultiplexer_2_out1, demultiplexer_3_out0,
       demultiplexer_3_out1, IDLE_2_q, IDLE_3_q, IDLE_4_q, IDLE_q, Lc, Lc_0, Ln, Ln_0, or_1_out;
  wire [23:0] bit_extender_1_out;
  wire [31:0] c, c___1, c___1_t, divider_1_rem, memory_1_data_out, multiplexer_1_out, multiplexer_2_out,
       multiplexer_3_out, n, n___10, n___10___48;

  Multiplexer #(.width(32), .enable("false")) multiplexer_1 (
    .in0(num), .in1(n___10), .out(multiplexer_1_out), .sel(Lc_0));
  Divider #(.width(32)) divider_1 (.a(n), .b(32'ha), .out(n___10), .rem(divider_1_rem));  // open: upper
  Adder #(.width(32)) adder_1 (.a(divider_1_rem), .b(32'h30), .out(n___10___48));  // open: cin, cout
  or or_1 (or_1_out, demultiplexer_1_out0, \end );
  Register #(.width(32)) u_n (.D(multiplexer_1_out), .en(Ln), .Q(n), .clk(CLK), .clr(RST));
  D_Flip_Flop IDLE (.clk(CLK), .D(or_1_out), .Q(IDLE_q), .preset(RST));  // open: Qn, en, reset
  Demultiplexer #(.enable("false")) demultiplexer_1 (
    .out0(demultiplexer_1_out0), .out1(Ln_0), .in(IDLE_q), .sel(start));
  or or_2 (Write_ASCII, demultiplexer_3_out0, demultiplexer_2_out1);
  Multiplexer #(.width(32), .enable("false")) multiplexer_2 (
    .in0(c___1), .in1(c___1_t), .out(multiplexer_2_out), .sel(Write_ASCII));
  Adder #(.width(32)) adder_2 (.a(c), .b(32'h1), .out(c___1));  // open: cin, cout
  Subtractor #(.width(32)) subtractor_1 (.a(c), .b(32'h1), .out(c___1_t));  // open: bin, bout
  D_Flip_Flop IDLE_2 (.clk(CLK), .D(Ln_0), .Q(IDLE_2_q), .reset(RST));  // open: Qn, preset, en
  Register #(.width(32)) u_c (.D(multiplexer_2_out), .en(Lc), .Q(c), .clk(CLK), .clr(RST));
  or or_3 (Lc_0, IDLE_2_q, demultiplexer_3_out1);
  Multiplexer #(.width(32), .enable("false")) multiplexer_3 (
    .in0(c), .in1(c___1_t), .out(multiplexer_3_out), .sel(Write_ASCII));
  Comparator #(.width(32), .mode("unsigned")) comparator_1 (.a({32{1'b0}}), .b(n), .lt(_0_n));  // open: gt, eq
  Comparator #(.width(32), .mode("unsigned")) comparator_2 (.a({32{1'b0}}), .b(c), .lt(_0_c));  // open: gt, eq
  D_Flip_Flop IDLE_3 (.clk(CLK), .D(Write_ASCII), .Q(IDLE_3_q), .reset(RST));  // open: Qn, preset, en
  Demultiplexer #(.enable("false")) demultiplexer_2 (
    .out0(demultiplexer_2_out0), .out1(demultiplexer_2_out1), .in(IDLE_3_q), .sel(_0_c));
  Bit_Extender #(.in_width(32), .out_width(24)) bit_extender_1 (.in(multiplexer_3_out), .out(bit_extender_1_out));
  D_Flip_Flop IDLE_4 (.clk(CLK), .D(Lc_0), .Q(IDLE_4_q), .reset(RST));  // open: Qn, preset, en
  or or_4 (Lc, Lc_0, Write_ASCII);
  or or_5 (Ln, Ln_0, Lc_0);
  Demultiplexer #(.enable("false")) demultiplexer_3 (
    .out0(demultiplexer_3_out0), .out1(demultiplexer_3_out1), .in(IDLE_4_q), .sel(_0_n));
  D_Flip_Flop IDLE_5 (.clk(CLK), .D(demultiplexer_2_out0), .Q(\end ), .reset(RST));  // open: Qn, preset, en
  MEMORY memory_1 (
    .DIR(bit_extender_1_out), .DATA_IN(n___10___48), .WRITE(Lc_0), .CLK(CLK), .CLR(RST),
    .DATA_OUT(memory_1_data_out));
  Bit_Extender #(.in_width(32), .out_width(7)) bit_extender_2 (.in(memory_1_data_out), .out(ASCII));

  // Other names for the same wires on the sheet: Lc_1 = Write_ASCII; Sc = Write_ASCII; Ln_1 = Lc_0; Sn = Lc_0;
  //   Write = Lc_0
endmodule

module PRINT_DEC (
  input  [31:0] num,
  input  start,
  input  CLK,
  input  RST,
  output [6:0] ASCII,
  output Write_ASCII,
  output END
);

  wire demultiplexer_1_out0, demultiplexer_1_out1, demultiplexer_2_out0, demultiplexer_3_out0, end_t,
       IDLE_3_q, IDLE_q, or_1_out, or_2_out, or_3_out, S_ASCII, startUDEC, Write_ASCII_1;
  wire [6:0] ASCII_t;
  wire [31:0] multiplexer_1_out, negator_1_out;

  or or_1 (or_1_out, demultiplexer_1_out0, END);
  Negator #(.width(32)) negator_1 (.in(num), .out(negator_1_out));
  D_Flip_Flop IDLE (.clk(CLK), .D(or_1_out), .Q(IDLE_q), .preset(RST));  // open: Qn, en, reset
  Demultiplexer #(.enable("false")) demultiplexer_1 (
    .out0(demultiplexer_1_out0), .out1(demultiplexer_1_out1), .in(IDLE_q), .sel(start));
  Multiplexer #(.width(32), .enable("false")) multiplexer_1 (
    .in0(num), .in1(negator_1_out), .out(multiplexer_1_out), .sel(num[31]));
  Demultiplexer #(.enable("false")) demultiplexer_2 (
    .out0(demultiplexer_2_out0), .out1(S_ASCII), .in(demultiplexer_1_out1), .sel(num[31]));
  or or_2 (or_2_out, demultiplexer_2_out0, S_ASCII);
  D_Flip_Flop IDLE_2 (.clk(CLK), .D(or_2_out), .Q(startUDEC), .reset(RST));  // open: Qn, preset, en
  PRINT_UDEC print_udec_1 (
    .num(multiplexer_1_out), .start(startUDEC), .CLK(CLK), .RST(RST), .ASCII(ASCII_t),
    .Write_ASCII(Write_ASCII_1), .\end (end_t));
  D_Flip_Flop IDLE_3 (.clk(CLK), .D(or_3_out), .Q(IDLE_3_q), .reset(RST));  // open: Qn, preset, en
  or or_3 (or_3_out, startUDEC, demultiplexer_3_out0);
  Demultiplexer #(.enable("false")) demultiplexer_3 (
    .out0(demultiplexer_3_out0), .out1(END), .in(IDLE_3_q), .sel(end_t));
  Multiplexer #(.width(7), .enable("false")) multiplexer_2 (
    .in0(ASCII_t), .in1(7'b0101101), .out(ASCII), .sel(S_ASCII));
  or or_4 (Write_ASCII, S_ASCII, Write_ASCII_1);

  // Other names for the same wires on the sheet: sign = num[31]; Write_ASCII_0 = S_ASCII
endmodule

module TEST_PRINT (
  input  [31:0] in_1,
  output out_2
);

  wire button_1_out, button_2_out, CLK, CLR, d_ff_1_q, Write_ASCII;
  wire [6:0] ASCII;

  Button button_1 (.out(button_1_out));
  Clock clock_1 (.out(CLK));
  D_Flip_Flop d_ff_1 (.clk(CLK), .D(1'b1), .Q(d_ff_1_q), .reset(button_1_out));  // open: Qn, preset, en
  D_Flip_Flop d_ff_2 (.clk(CLK), .D(d_ff_1_q), .Qn(CLR), .reset(button_1_out));  // open: Q, preset, en
  Button button_2 (.out(button_2_out));
  PRINT_UDEC print_udec_1 ();  // open: num, start, CLK, RST, ASCII, Write_ASCII, end
  PRINT_DEC print_dec_1 (
    .num(in_1), .start(button_2_out), .CLK(CLK), .RST(CLR), .ASCII(ASCII), .Write_ASCII(Write_ASCII),
    .END(out_2));
  TTY #(.rows(32), .cols(60)) tty_1 (.data(ASCII), .clk(CLK), .we(Write_ASCII), .clr(CLR));
endmodule

module DataPath (
  input  [31:0] Input,
  input  Mod_M,
  input  Cont_Lec,
  input  CLK,
  input  CLR,
  input  Max_Dec,
  input  [1:0] SI,
  input  [1:0] SJ,
  input  [31:0] in_9,
  input  [31:0] in_10,
  output Cond_3,
  output [31:0] Lectura2,
  output Array_Guardado,
  output Cond_1,
  output Cond_2,
  output [31:0] out_16,
  output [31:0] out_17,
  output Condicional_Interna,
  output [31:0] out_19,
  output [31:0] out_20,
  output [31:0] out_21
);

  wire aux_count, aux_count_1, comparator_3_lt, comparator_4_eq, comparator_4_lt, comparator_5_eq,
       comparator_6_eq, comparator_7_eq, comparator_7_lt, comparator_8_eq, comparator_9_eq,
       controlled_buffer_7_out, controlled_buffer_10_out, controlled_buffer_11_out, New_Max, not_1_out,
       not_2_out, not_3_out, not_4_out, not_5_out, not_6_out, not_7_out, not_8_out, stop;
  wire [4:0] count, count_1, Lec_Array_2;
  wire [31:0] bit_extender_1_out, bit_extender_2_out, Columna, controlled_buffer_1_out,
       controlled_buffer_2_out, controlled_buffer_3_out, controlled_buffer_4_out, demultiplexer_1_out0,
       demultiplexer_1_out1, demultiplexer_2_out0, demultiplexer_2_out1, Fila, I, I___1, Index, Input_I,
       Input_J, Input_M, Input_Max, Input_Max_Aux, J, J___1, Lectura_1, Len_1, Len_2, M, Matrix_Out, Max,
       Max___1, Max_I, Max_I_Input, Max_J, Max_J_Input, N;
  wire [31:5] multiplexer_5_out;

  assign controlled_buffer_1_out = not_1_out ? Input : 32'bz;  // Controlled_Buffer controlled_buffer_1
  not not_1 (not_1_out, stop);
  assign controlled_buffer_2_out = not_2_out ? Input : 32'bz;  // Controlled_Buffer controlled_buffer_2
  not not_2 (not_2_out, Array_Guardado);
  Multiplexer #(.select(2), .width(32), .enable("false")) multiplexer_1 (
    .in0(I), .in1(I___1), .in2(32'h1), .out(Input_I), .sel(SI));  // open: in3
  Multiplexer #(.width(32), .enable("false")) multiplexer_2 (.in0(I), .in1(out_16), .out(Fila), .sel(not_3_out));
  not not_3 (not_3_out, Mod_M);
  Multiplexer #(.width(32), .enable("false")) multiplexer_3 (.in0(J), .in1(out_17), .out(Columna), .sel(not_4_out));
  not not_4 (not_4_out, Mod_M);
  Demultiplexer #(.width(32), .enable("false")) demultiplexer_1 (
    .out0(demultiplexer_1_out0), .out1(demultiplexer_1_out1), .in(controlled_buffer_1_out), .sel(aux_count));
  Demultiplexer #(.width(32), .enable("false")) demultiplexer_2 (
    .out0(demultiplexer_2_out0), .out1(demultiplexer_2_out1), .in(controlled_buffer_2_out), .sel(aux_count_1));
  assign controlled_buffer_3_out = not_5_out ? demultiplexer_1_out0 : 32'bz;  // Controlled_Buffer controlled_buffer_3
  not not_5 (not_5_out, aux_count);
  assign controlled_buffer_4_out = not_6_out ? demultiplexer_2_out0 : 32'bz;  // Controlled_Buffer controlled_buffer_4
  Register #(.width(32)) register_1 (.D(controlled_buffer_4_out), .Q(M), .clk(CLK));  // open: en, clr
  not not_6 (not_6_out, aux_count_1);
  Multiplexer #(.select(2), .width(32), .enable("false")) multiplexer_4 (
    .in0(J), .in1(J___1), .in2(32'h1), .out(Input_J), .sel(SJ));  // open: in3
  Multiplexer #(.width(32), .enable("false")) multiplexer_5 (
    .in0(out_17), .in1(Index), .out({multiplexer_5_out, Lec_Array_2}), .sel(Cont_Lec));
  Multiplexer #(.width(32), .enable("false")) multiplexer_6 (
    .in0(Input_Max_Aux), .in1(Max___1), .out(Input_Max), .sel(Max_Dec));
  Comparator #(.width(32), .mode("unsigned")) comparator_1 (.a(Max), .b({32{1'b0}}), .gt(Cond_3));  // open: eq, lt
  Register #(.width(32)) register_2 (.D(controlled_buffer_3_out), .Q(N), .clk(CLK));  // open: en, clr
  D_Flip_Flop d_ff_1 (.clk(CLK), .D(1'b1), .Q(aux_count));  // open: Qn, preset, en, reset
  Comparator #(.width(32), .mode("unsigned")) comparator_2 (
    .a(Lectura_1), .b(Lectura2), .eq(Condicional_Interna));  // open: gt, lt
  Comparator #(.width(32), .mode("unsigned")) comparator_3 (
    .a(Max), .b(Input_M), .lt(comparator_3_lt));  // open: gt, eq
  Adder #(.width(32)) adder_1 (.a(Matrix_Out), .b(32'h1), .out(out_19));  // open: cin, cout
  assign Input_M = Mod_M ? out_19 : 32'bz;  // Controlled_Buffer controlled_buffer_5
  assign Input_Max_Aux = New_Max ? Input_M : 32'bz;  // Controlled_Buffer controlled_buffer_6
  and and_1 (New_Max, comparator_3_lt, Mod_M);
  Subtractor #(.width(32)) subtractor_1 (.a(Max_J), .b(Max), .out(Index));  // open: bin, bout
  Subtractor #(.width(32)) subtractor_2 (.a(Max), .b(32'h1), .out(Max___1));  // open: bin, bout
  RegisterFile_main main_1 (
    .Selector_de_Registro(count), .Entrada(demultiplexer_1_out1), .Lectura_R1(out_16[4:0]),
    .out_5(Lectura_1), .in_3(CLK));
  RegisterFile_main main_2 (
    .Selector_de_Registro(count_1), .Entrada(demultiplexer_2_out1), .Lectura_R1(Lec_Array_2),
    .out_5(Lectura2), .in_3(CLK));
  Counter #(.width(5), .max('h1f)) counter_1 (
    .Q(count), .clk(controlled_buffer_7_out));  // open: load, D, count, carry, clr
  assign controlled_buffer_7_out = aux_count ? CLK : 1'bz;  // Controlled_Buffer controlled_buffer_7
  Comparator #(.width(32), .mode("unsigned")) comparator_4 (
    .a(I), .b(N), .eq(comparator_4_eq), .lt(comparator_4_lt));  // open: gt
  or or_1 (Cond_1, comparator_4_eq, comparator_4_lt);
  assign Max_I_Input = New_Max ? I : 32'bz;  // Controlled_Buffer controlled_buffer_8
  assign Max_J_Input = New_Max ? J : 32'bz;  // Controlled_Buffer controlled_buffer_9
  assign bit_extender_1_out = {{27{1'b0}}, count};  // Bit_Extender bit_extender_1
  Register #(.width(32)) u_Len_1 (.Q(Len_1), .clk(CLK), .clr(CLR));  // open: D, en
  Comparator #(.width(32), .mode("unsigned")) comparator_5 (
    .a(N), .b(bit_extender_1_out), .eq(comparator_5_eq));  // open: gt, lt
  Comparator #(.width(32), .mode("unsigned")) comparator_6 (
    .a(bit_extender_1_out), .b({32{1'b0}}), .eq(comparator_6_eq));  // open: gt, lt
  not not_7 (not_7_out, comparator_6_eq);
  or or_2 (Cond_2, comparator_7_eq, comparator_7_lt);
  Comparator #(.width(32), .mode("unsigned")) comparator_7 (
    .a(J), .b(M), .eq(comparator_7_eq), .lt(comparator_7_lt));  // open: gt
  Subtractor #(.width(32)) subtractor_3 (.a(I), .b(32'h1), .out(out_16));  // open: bin, bout
  Matrix matrix_1 (
    .in_1(CLK), .Fila(Fila), .Columna(Columna), .Input(Input_M), .in_3(Mod_M), .Salida(out_20),
    .Salida_Comp(out_21), .Columna___1(out_17), .Fila___1(out_16));  // open: out_10, out_11
  Register #(.width(32)) u_I (.D(Input_I), .Q(I), .clk(CLK), .clr(CLR));  // open: en
  and and_2 (stop, comparator_5_eq, not_7_out);
  assign bit_extender_2_out = {{27{1'b0}}, count_1};  // Bit_Extender bit_extender_2
  Register #(.width(32)) u_J (.D(Input_J), .Q(J), .clk(CLK), .clr(CLR));  // open: en
  Register #(.width(32)) u_Len_2 (.Q(Len_2), .clk(CLK), .clr(CLR));  // open: D, en
  Comparator #(.width(32), .mode("unsigned")) comparator_8 (
    .a(M), .b(bit_extender_2_out), .eq(comparator_8_eq));  // open: gt, lt
  Comparator #(.width(32), .mode("unsigned")) comparator_9 (
    .a(bit_extender_2_out), .b({32{1'b0}}), .eq(comparator_9_eq));  // open: gt, lt
  not not_8 (not_8_out, comparator_9_eq);
  Subtractor #(.width(32)) subtractor_4 (.a(J), .b(32'h1), .out(out_17));  // open: bin, bout
  Register #(.width(32)) u_Max (.D(Input_Max), .Q(Max), .clk(CLK), .clr(CLR));  // open: en
  and and_3 (Array_Guardado, comparator_8_eq, not_8_out);
  Register #(.width(32)) register_3 (.D(out_20), .Q(Matrix_Out), .clk(CLK));  // open: en, clr
  // OR_Gate or_3 is placed but not wired
  Adder #(.width(32)) adder_2 (.a(I), .b(32'h1), .out(I___1));  // open: cin, cout
  Register #(.width(32)) u_Max_I (.D(Max_I_Input), .Q(Max_I), .clk(CLK), .clr(CLR));  // open: en
  Counter #(.width(5), .max('h1f)) counter_2 (
    .Q(count_1), .clk(controlled_buffer_10_out));  // open: load, D, count, carry, clr
  assign controlled_buffer_10_out = aux_count_1 ? CLK : 1'bz;  // Controlled_Buffer controlled_buffer_10
  Adder #(.width(32)) adder_3 (.a(J), .b(32'h1), .out(J___1));  // open: cin, cout
  assign controlled_buffer_11_out = stop ? CLK : 1'bz;  // Controlled_Buffer controlled_buffer_11
  D_Flip_Flop d_ff_2 (.clk(controlled_buffer_11_out), .D(1'b1), .Q(aux_count_1));  // open: Qn, preset, en, reset
  Register #(.width(32)) u_Max_J (.D(Max_J_Input), .Q(Max_J), .clk(CLK), .clr(CLR));  // open: en

  // Other names for the same wires on the sheet: _1er_ciclo = Cond_1; _2do_ciclo = Cond_2; C_Lec = Cont_Lec;
  //   Dec_Max = Max_Dec; I___1_t[31:0] = out_16; J___1_t[31:0] = out_17; Lec_Array_1[4:0] = out_16[4:0];
  //   Lectura_2[31:0] = Lectura2; Matrix_Out_Aux[31:0] = out_20; Mod = Mod_M; new_value[31:0] = Input_M;
  //   stop_1 = Array_Guardado

  // Notes on the sheet:
  //   Modificando la matriz
  //   Array 2
  //   Array 1
  //   Matriz
endmodule

module ControlUnit (
  input  CLK,
  input  Start,
  input  Cond1,
  input  Cond2,
  input  Cond_int,
  input  Cond_3,
  input  RST,
  input  EndPrint,
  output Mod_M,
  output [1:0] SI,
  output [1:0] SJ,
  output Dec_Max,
  output RSTPrint,
  output StartPrint,
  output Cont_Lec,
  output END
);

  wire d_ff_1_q, d_ff_2_q, d_ff_3_q, d_ff_4_q, d_ff_5_q, d_ff_6_q, demultiplexer_1_out0,
       demultiplexer_2_out0, demultiplexer_3_out0, demultiplexer_4_out0, demultiplexer_5_out1,
       demultiplexer_6_out0, or_1_out, or_2_out, or_3_out, or_5_out, or_6_out;

  D_Flip_Flop d_ff_1 (.clk(CLK), .D(demultiplexer_1_out0), .Q(d_ff_1_q), .preset(RST));  // open: Qn, en, reset
  Demultiplexer #(.enable("false")) demultiplexer_1 (
    .out0(demultiplexer_1_out0), .out1(SI[1]), .in(d_ff_1_q), .sel(Start));
  or or_1 (or_1_out, SI[0], SI[1]);
  D_Flip_Flop d_ff_2 (.clk(CLK), .D(or_1_out), .Q(d_ff_2_q));  // open: Qn, preset, en, reset
  Demultiplexer #(.enable("false")) demultiplexer_2 (
    .out0(demultiplexer_2_out0), .out1(SJ[1]), .in(d_ff_2_q), .sel(Cond1));
  D_Flip_Flop d_ff_3 (.clk(CLK), .D(or_2_out), .Q(d_ff_3_q));  // open: Qn, preset, en, reset
  or or_2 (or_2_out, Dec_Max, demultiplexer_2_out0);
  or or_3 (or_3_out, SJ[0], SJ[1]);
  Demultiplexer #(.enable("false")) demultiplexer_3 (
    .out0(demultiplexer_3_out0), .out1(Cont_Lec), .in(d_ff_3_q), .sel(Cond_3));
  D_Flip_Flop d_ff_4 (.clk(CLK), .D(or_3_out), .Q(d_ff_4_q));  // open: Qn, preset, en, reset
  D_Flip_Flop d_ff_5 (.clk(CLK), .D(d_ff_4_q), .Q(d_ff_5_q));  // open: Qn, preset, en, reset
  D_Flip_Flop d_ff_6 (.clk(CLK), .D(StartPrint), .Q(d_ff_6_q), .reset(RST));  // open: Qn, preset, en
  or or_4 (StartPrint, demultiplexer_4_out0, Cont_Lec);
  Demultiplexer #(.enable("false")) demultiplexer_4 (
    .out0(demultiplexer_4_out0), .out1(Dec_Max), .in(d_ff_6_q), .sel(EndPrint));
  Demultiplexer #(.enable("false")) demultiplexer_5 (
    .out0(SI[0]), .out1(demultiplexer_5_out1), .in(d_ff_5_q), .sel(Cond2));
  or or_5 (or_5_out, END, demultiplexer_3_out0);
  Demultiplexer #(.enable("false")) demultiplexer_6 (
    .out0(demultiplexer_6_out0), .out1(Mod_M), .in(demultiplexer_5_out1), .sel(Cond_int));
  D_Flip_Flop d_ff_7 (.clk(CLK), .D(or_5_out), .Q(END));  // open: Qn, preset, en, reset
  or or_6 (or_6_out, demultiplexer_6_out0, Mod_M);
  D_Flip_Flop d_ff_8 (.clk(CLK), .D(or_6_out), .Q(SJ[0]));  // open: Qn, preset, en, reset

  assign RSTPrint = Dec_Max;

  // Other names for the same wires on the sheet: cond_1 = Cond1; cond_2 = Cond2; Mod = Mod_M

  // Notes on the sheet:
  //   Mod M
  //   Inc I
  //   Inc J
  //   Fin de ambos ciclos
  //   Cod Interno
endmodule

module Matrix (
  input  in_1,
  input  [31:0] Input,
  input  in_3,
  input  [31:0] Fila,
  input  [31:0] Columna,
  input  [31:0] Fila___1,
  input  [31:0] Columna___1,
  output [31:0] Salida,
  output [31:0] Salida_Comp,
  output [4:0] out_10,
  output [4:0] out_11
);

  wire [4:0] _1, _2, _3, _4, _5, _6, _7, _8, _9, _10, _11, _12, _13, _14, _15, _16, _17, _18, _19, _20, _21,
       _22, _23, _24, _25, _26, _27, _28, _29, _30, _31, _32;
  wire [31:0] Input_t, Out_1, Out_2, Out_3, Out_4, Out_5, Out_6, Out_7, Out_8, Out_9, Out_10_t, Out_11_t,
       Out_12, Out_13, Out_14, Out_15, Out_16, Out_17, Out_18, Out_19, Out_20, Out_21, Out_22, Out_23,
       Out_24, Out_25, Out_26, Out_27, Out_28, Out_29, Out_30, Out_31, Out_32, Out__5;

  Demultiplexer #(.select(5), .width(5), .enable("false")) demultiplexer_1 (
    .out0(_1), .out1(_2), .out2(_3), .out3(_4), .out4(_5), .out5(_6), .out6(_7), .out7(_8), .out8(_9),
    .out9(_10), .out10(_11), .out11(_12), .out12(_13), .out13(_14), .out14(_15), .out15(_16), .out16(_17),
    .out17(_18), .out18(_19), .out19(_20), .out20(_21), .out21(_22), .out22(_23), .out23(_24), .out24(_25),
    .out25(_26), .out26(_27), .out27(_28), .out28(_29), .out29(_30), .out30(_31), .out31(_32),
    .in(Columna[4:0]), .sel(Fila[4:0]));
  assign Input_t = in_3 ? Input : 32'bz;  // Controlled_Buffer controlled_buffer_1
  Multiplexer #(.select(5), .width(32), .enable("false")) multiplexer_1 (
    .in0(Out_1), .in1(Out_2), .in2(Out_3), .in3(Out_4), .in4(Out_5), .in5(Out_6), .in6(Out_7), .in7(Out_8),
    .in8(Out_9), .in9(Out_10_t), .in10(Out_11_t), .in11(Out_13), .in12(Out_12), .in13(Out_14), .in14(Out_15),
    .in15(Out_16), .in16(Out_17), .in17(Out_18), .in18(Out_19), .in19(Out_20), .in20(Out_21), .in21(Out_22),
    .in22(Out_23), .in23(Out_24), .in24(Out_25), .in25(Out_26), .in26(Out_27), .in27(Out_28), .in28(Out_29),
    .in29(Out_30), .in30(Out_31), .in31(Out_32), .out(Salida), .sel(Fila[4:0]));
  Multiplexer #(.select(5), .width(32), .enable("false")) multiplexer_2 (
    .in0(Out_1), .in1(Out_2), .in2(Out_3), .in3(Out_4), .in4(Out_5), .in5(Out_6), .in6(Out_7), .in7(Out_8),
    .in8(Out_9), .in9(Out_10_t), .in10(Out_11_t), .in11(Out_13), .in12(Out_12), .in13(Out_14), .in14(Out_15),
    .in15(Out_16), .in16(Out_17), .in17(Out_18), .in18(Out_19), .in19(Out_20), .in20(Out_21), .in21(Out_22),
    .in22(Out_23), .in23(Out_24), .in24(Out_25), .in25(Out_26), .in26(Out_27), .in27(Out_28), .in28(Out_29),
    .in29(Out_30), .in30(Out_31), .in31(Out_32), .out(Salida_Comp), .sel(Fila___1[4:0]));
  RegisterFile_main main_1 (.Selector_de_Registro(_1), .Entrada(Input_t), .Lectura_R1(_1), .out_5(Out_1), .in_3(in_1));
  RegisterFile_main main_2 (.Selector_de_Registro(_2), .Entrada(Input_t), .Lectura_R1(_2), .out_5(Out_2), .in_3(in_1));
  RegisterFile_main main_3 (.Selector_de_Registro(_3), .Entrada(Input_t), .Lectura_R1(_3), .out_5(Out_3), .in_3(in_1));
  RegisterFile_main main_4 (.Selector_de_Registro(_4), .Entrada(Input_t), .Lectura_R1(_4), .out_5(Out_4), .in_3(in_1));
  RegisterFile_main main_5 (.Selector_de_Registro(_5), .Entrada(Input_t), .Lectura_R1(_5), .out_5(Out__5), .in_3(in_1));
  RegisterFile_main main_6 (.Selector_de_Registro(_6), .Entrada(Input_t), .Lectura_R1(_6), .out_5(Out_6), .in_3(in_1));
  RegisterFile_main main_7 (.Selector_de_Registro(_7), .Entrada(Input_t), .Lectura_R1(_7), .out_5(Out_7), .in_3(in_1));
  RegisterFile_main main_8 (.Selector_de_Registro(_8), .Entrada(Input_t), .Lectura_R1(_8), .out_5(Out_8), .in_3(in_1));
  RegisterFile_main main_9 (.Selector_de_Registro(_9), .Entrada(Input_t), .Lectura_R1(_9), .out_5(Out_9), .in_3(in_1));
  RegisterFile_main main_10 (
    .Selector_de_Registro(_10), .Entrada(Input_t), .Lectura_R1(_10), .out_5(Out_10_t), .in_3(in_1));
  RegisterFile_main main_11 (
    .Selector_de_Registro(_11), .Entrada(Input_t), .Lectura_R1(_11), .out_5(Out_11_t), .in_3(in_1));
  RegisterFile_main main_12 (
    .Selector_de_Registro(_12), .Entrada(Input_t), .Lectura_R1(_12), .out_5(Out_12), .in_3(in_1));
  RegisterFile_main main_13 (
    .Selector_de_Registro(_13), .Entrada(Input_t), .Lectura_R1(_13), .out_5(Out_13), .in_3(in_1));
  RegisterFile_main main_14 (
    .Selector_de_Registro(_14), .Entrada(Input_t), .Lectura_R1(_14), .out_5(Out_14), .in_3(in_1));
  RegisterFile_main main_15 (
    .Selector_de_Registro(_15), .Entrada(Input_t), .Lectura_R1(_15), .out_5(Out_15), .in_3(in_1));
  RegisterFile_main main_16 (
    .Selector_de_Registro(_16), .Entrada(Input_t), .Lectura_R1(_16), .out_5(Out_16), .in_3(in_1));
  RegisterFile_main main_17 (
    .Selector_de_Registro(_17), .Entrada(Input_t), .Lectura_R1(_17), .out_5(Out_17), .in_3(in_1));
  RegisterFile_main main_18 (
    .Selector_de_Registro(_18), .Entrada(Input_t), .Lectura_R1(_18), .out_5(Out_18), .in_3(in_1));
  RegisterFile_main main_19 (
    .Selector_de_Registro(_19), .Entrada(Input_t), .Lectura_R1(_19), .out_5(Out_19), .in_3(in_1));
  RegisterFile_main main_20 (
    .Selector_de_Registro(_20), .Entrada(Input_t), .Lectura_R1(_20), .out_5(Out_20), .in_3(in_1));
  RegisterFile_main main_21 (
    .Selector_de_Registro(_21), .Entrada(Input_t), .Lectura_R1(_21), .out_5(Out_21), .in_3(in_1));
  RegisterFile_main main_22 (
    .Selector_de_Registro(_22), .Entrada(Input_t), .Lectura_R1(_22), .out_5(Out_22), .in_3(in_1));
  RegisterFile_main main_23 (
    .Selector_de_Registro(_23), .Entrada(Input_t), .Lectura_R1(_23), .out_5(Out_23), .in_3(in_1));
  RegisterFile_main main_24 (
    .Selector_de_Registro(_24), .Entrada(Input_t), .Lectura_R1(_24), .out_5(Out_24), .in_3(in_1));
  RegisterFile_main main_25 (
    .Selector_de_Registro(_25), .Entrada(Input_t), .Lectura_R1(_25), .out_5(Out_25), .in_3(in_1));
  RegisterFile_main main_26 (
    .Selector_de_Registro(_26), .Entrada(Input_t), .Lectura_R1(_26), .out_5(Out_26), .in_3(in_1));
  RegisterFile_main main_27 (
    .Selector_de_Registro(_27), .Entrada(Input_t), .Lectura_R1(_28), .out_5(Out_27), .in_3(in_1));
  RegisterFile_main main_28 (
    .Selector_de_Registro(_28), .Entrada(Input_t), .Lectura_R1(_28), .out_5(Out_28), .in_3(in_1));
  RegisterFile_main main_29 (
    .Selector_de_Registro(_29), .Entrada(Input_t), .Lectura_R1(_29), .out_5(Out_29), .in_3(in_1));
  RegisterFile_main main_30 (
    .Selector_de_Registro(_30), .Entrada(Input_t), .Lectura_R1(_30), .out_5(Out_30), .in_3(in_1));
  RegisterFile_main main_31 (
    .Selector_de_Registro(_31), .Entrada(Input_t), .Lectura_R1(_31), .out_5(Out_31), .in_3(in_1));
  RegisterFile_main main_32 (
    .Selector_de_Registro(_32), .Entrada(Input_t), .Lectura_R1(_32), .out_5(Out_32), .in_3(in_1));

  assign out_10 = Fila[4:0];
  assign out_11 = Columna[4:0];

  // Other names for the same wires on the sheet: CLK = in_1; Columna___1_t[4:0] = Columna___1[4:0];
  //   Columna_t[4:0] = Columna[4:0]; Enable = in_3; Fila___1_t[4:0] = Fila___1[4:0]; Fila_t[4:0] = Fila[4:0];
  //   Out[31:0] = Salida; Out_i_1_j_1[31:0] = Salida_Comp
endmodule
